# Fritzing sketch AirQuality (saved by Fritzing 0.9.3b)

parts:
  Part1 = Adafruit HDC1008 Temperature Humidity Sensor [part_number="Adafruit #2635"]
  U1 = SUP500F [package=sup500f]  # not connected
  Part2 = Arduino Uno (Rev3)
  U2 = PIC-ICSP [package=molex-1x6]
  JP1 = Header 8 [package=bm08b-srss-tb]

nets:
  VDD: Part1.VDD, Part2.5V
  GND: Part1.GND, Part2.GND
  N1: Part1.SCL, Part2.A5/SCL
  N2: Part1.SDA, Part2.A4/SDA
  N3: U2.PGC, JP1.6
  N4: U2.GND, JP1.7
  N5: U2.VCC, JP1.8

notes:
  TX
  RX
  GND
  5V
  SDS011 Sensor connection
  The sensor is meant to be connected to the UART port in the senseBox Shield
  this is an schema of how it works

custom parts:
  Adafruit HDC1008 Temperature Humidity Sensor: This I2C digital humidity sensor is a fairly accurate and intelligent alternative to the much simpler Humidity and Temperature Sensor - SHT15 Breakout It has a typical accuracy of ±4% with an operating range that's optimized from 10% to 80% RH. Operation outside this range is still possible - just the accuracy might drop a bit. The temperature output has a typical accuracy of ±0.2°C from -20~85°C.
